# Fritzing sketch bb01v01 (saved by Fritzing 0.9.3b)
breadboards: 1

parts:
  U1 = Adafruit Trinket 5V
  U2 = NeoPixel Jewel [part_number=2226]
  U3 = NeoPixel Jewel [part_number=2226]
  R1 = Resistor [tolerance=±5% resistance=470 package="2010 [SMD]"]
  C1 = Electrolytic Capacitor [capacitance=1mF package="200 mil [THT, electrolytic]"]
  BATT1 = 3xAAA Switchable Battery Pack w/Bare Wire
  S3 = SPST Switch [package=switch-spdt_lock.007s]
  MIC1 = Microphone
  R7 = Resistor [tolerance=±5% resistance=10k package="0805 [SMD]"]
  S5 = Pushbutton [package="[THT]"]
  S7 = Pushbutton [package="[THT]"]
  R8 = Resistor [tolerance=±5% resistance=10k package="0805 [SMD]"]
  R9 = Resistor [tolerance=±5% resistance=10k package="0805 [SMD]"]

nets:
  VDD: U1.VBAT, U2.VDD, U3.VDD, C1.+, S3.O, S5.Pin_3, S5.Pin_4, S7.Pin_3, S7.Pin_4
  GND: U1.GND, U2.GND, U3.GND, C1.-, BATT1.NEG, S3.P, MIC1.pin1
  N1: U1.#1, S5.Pin_1, S5.Pin_2, R8.Pin_0
  N2: U1.#2, S7.Pin_1, S7.Pin_2, R9.Pin_0
  N3: U1.#0, R1.Pin_0
  N4: U1.#3, MIC1.pin2, R7.Pin_0
  N5: U2.IN, R1.Pin_1
  N6: U2.OUT, U3.IN
  N7: BATT1.POS, S3.S

custom parts:
  Adafruit Trinket 5V: Trinket may be small, but do not be fooled by its size! It's a tiny microcontroller board, built around the Atmel ATtiny85, a little chip with a lot of power. We wanted to design a microcontroller board that was small enough to fit into any project, and low cost enough to use without hesitation. Perfect for when you don't want to give up your expensive dev-board and you aren't willing to take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
  NeoPixel Jewel: We fit seven of our tiny 5050 (5mm x 5mm) smart RGB LEDs onto a beautiful, round PCB with mounting holes and a chainable design to create what we think is our most elegant (and evening-wear appropriate) NeoPixel board yet. Use only one microcontroller pin to control as many as you can chain together! Each LED is addressable as the driver chip is inside the LED. Each one has ~18mA constant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
  3xAAA Switchable Battery Pack w/Bare Wire: 3xAAA Switchable Battery Pack w/Bare Wire Connectors
